// Digital circuit 5bitPc0.dig as structural Verilog
module _5bitPc0 (
  input  Re_a,
  output AI0,
  output AI1,
  output AI2,
  output AI3
);

  wire and_3_out, and_5_out, and_7_out, and_9_out, jk_ff_as_1_q, jk_ff_as_2_q, jk_ff_as_3_q, jk_ff_as_4_q,
       jk_ff_as_5_q, undriven, undriven_2, undriven_3, undriven_4, undriven_5, undriven_6, undriven_7,
       undriven_8, undriven_9;
  wire [3:0] pullup_1_out;

  // And and_1 is placed but not wired
  // And and_2 is placed but not wired
  and and_3 (and_3_out, undriven_9, jk_ff_as_1_q);
  JK_FF_AS jk_ff_as_1 (
    .Set(undriven_7), .J(undriven_9), .C(undriven_4), .K(undriven_9), .Clr(undriven_2), .Q(jk_ff_as_1_q));  // open: nQ
  assign AI0 = undriven_8 ? jk_ff_as_1_q : 1'bz;  // Driver driver_1
  // And and_4 is placed but not wired
  and and_5 (and_5_out, undriven_9, and_3_out, jk_ff_as_2_q);
  JK_FF_AS jk_ff_as_2 (
    .Set(undriven_6), .J(and_3_out), .C(undriven_4), .K(and_3_out), .Clr(undriven_2), .Q(jk_ff_as_2_q));  // open: nQ
  assign AI1 = undriven_8 ? jk_ff_as_2_q : 1'bz;  // Driver driver_2
  // And and_6 is placed but not wired
  and and_7 (and_7_out, undriven_9, and_5_out, jk_ff_as_3_q);
  JK_FF_AS jk_ff_as_3 (
    .Set(undriven_5), .J(and_5_out), .C(undriven_4), .K(and_5_out), .Clr(undriven_2), .Q(jk_ff_as_3_q));  // open: nQ
  assign AI2 = undriven_8 ? jk_ff_as_3_q : 1'bz;  // Driver driver_3
  // And and_8 is placed but not wired
  and and_9 (and_9_out, undriven_9, and_7_out, jk_ff_as_4_q);
  JK_FF_AS jk_ff_as_4 (
    .Set(undriven_3), .J(and_7_out), .C(undriven_4), .K(and_7_out), .Clr(undriven_2), .Q(jk_ff_as_4_q));  // open: nQ
  assign AI3 = undriven_8 ? jk_ff_as_4_q : 1'bz;  // Driver driver_4
  JK_FF_AS jk_ff_as_5 (
    .Set(and_9_out), .J(undriven), .C(undriven_4), .K(undriven), .Clr(undriven_2), .Q(jk_ff_as_5_q));  // open: nQ
  PullUp #(.Bits(4)) pullup_1 (.out(pullup_1_out));
  Seven_Seg_Hex seven_seg_hex_1 ();  // open: d, dp
endmodule
