// Digital circuit DffwEna.dig as structural Verilog
module DffwEna (
  input  D,
  input  E_out,
  input  E_in,
  output Q
);

  wire and_1_out, and_2_out, not_1_out, rs_ff_as_1_q;

  not not_1 (not_1_out, D);
  and and_1 (and_1_out, D, E_in);
  and and_2 (and_2_out, not_1_out, E_in);
  RS_FF_AS rs_ff_as_1 (.S(and_1_out), .R(and_2_out), .Q(rs_ff_as_1_q));  // open: nQ
  assign Q = E_out ? rs_ff_as_1_q : 1'bz;  // Driver driver_1
endmodule
