// Digital circuit mainBus.dig as structural Verilog
module mainBus (
  input  Base_Clk
);

  wire ACC_e, ADDRRam_e, ALU_CYin, ALU_INV, ALU_OUTe, ALU_RSLTe, ALU_SUB, and_1_out, and_2_out, DIRECTAddr_e,
       FLG_neg, FLG_z, IO_e, IORD_e, IOWR_e, JMP_e, JNEG_e, JZ_e, not_1_out, NXT_I, or_2_out, PCCNT_e,
       PCLD_e, PCOUT_e, RAM_e, RAMRD_e, RAMWR_e, RESET_out, RInst_E, RST, WR_nRD_e;
  wire [2:0] counter_1_out;
  wire [3:0] Acc_W_q_x, Acc_W_q_x_2, PGM_mem_d;
  wire [7:0] _5bitpc2_1_pc_out, ALU_dsp, Reg_B_q_x, Reg_I_2_q_x, Reg_I_q_x;
  wire [11:4] PGM_mem_d_2;

  and and_1 (and_1_out, JZ_e, FLG_z);
  and and_2 (and_2_out, JNEG_e, FLG_neg);
  Button RESET (.out(RESET_out));
  D_FF_AS d_ff_as_1 (.Set(RESET_out), .D(1'b0), .C(Base_Clk), .Clr(1'b0), .Q(RST));  // open: nQ
  or or_1 (PCLD_e, and_1_out, JMP_e, and_2_out);
  LED led_1 (.in(PCCNT_e));
  LED led_2 (.in(PCOUT_e));
  or or_2 (or_2_out, RST, NXT_I);
  _5bitPC2 _5bitpc2_1 (
    .PC_in(_5bitpc2_1_pc_out), .Le_a(PCLD_e), .CNTe_a(PCCNT_e), .CLK(Base_Clk), .CLR(RST), .Re_a(PCOUT_e),
    .PC_out(_5bitpc2_1_pc_out));
  Counter #(.Bits(3)) counter_1 (.en(1'b1), .C(Base_Clk), .clr(or_2_out), .out(counter_1_out));  // open: ovf
  Seven_Seg_Hex seven_seg_hex_1 (.d(PGM_mem_d), .dp(1'b0));
  sapRegX Reg_I (.E_in(RInst_E), .D_x(_5bitpc2_1_pc_out), .E_out(1'b1), .Q_x(Reg_I_q_x));
  ROM #(.AddrBits(6), .Bits(12)) PGM_mem (.A(Reg_I_q_x[5:0]), .sel(1'b1), .D({PGM_mem_d_2, PGM_mem_d}));
  assign _5bitpc2_1_pc_out = DIRECTAddr_e ? PGM_mem_d_2 : 8'bz;  // Driver driver_1
  LookUpTable #(.Bits(18)) MicroCodigo (
    .in0(counter_1_out[0]), .in1(counter_1_out[1]), .in2(counter_1_out[2]), .in3(PGM_mem_d[0]),
    .in4(PGM_mem_d[1]), .in5(PGM_mem_d[2]), .in6(PGM_mem_d[3]),
    .out({JNEG_e, JZ_e, WR_nRD_e, ALU_CYin, ALU_INV, ALU_SUB, IO_e, RAM_e, ALU_OUTe, ALU_RSLTe, ACC_e, ADDRRam_e, DIRECTAddr_e, RInst_E, NXT_I, PCOUT_e, PCCNT_e, JMP_e}));
  not not_1 (not_1_out, WR_nRD_e);
  Seven_Seg_Hex seven_seg_hex_2 (.d({2'b00, Reg_I_q_x[5:4]}), .dp(1'b0));
  Seven_Seg_Hex seven_seg_hex_3 (.d(Reg_I_q_x[3:0]), .dp(1'b0));
  Seven_Seg_Hex seven_seg_hex_4 (.d({1'b0, counter_1_out}), .dp(1'b0));
  and and_3 (RAMWR_e, WR_nRD_e, RAM_e);
  and and_4 (RAMRD_e, RAM_e, not_1_out);
  and and_5 (IOWR_e, WR_nRD_e, IO_e);
  and and_6 (IORD_e, IO_e, not_1_out);
  Seven_Seg_Hex seven_seg_hex_5 (.d(_5bitpc2_1_pc_out[7:4]), .dp(1'b0));
  Seven_Seg_Hex seven_seg_hex_6 (.d(_5bitpc2_1_pc_out[3:0]), .dp(1'b0));
  Seven_Seg_Hex seven_seg_hex_7 (.d(Acc_W_q_x_2), .dp(1'b0));
  sapRegX Acc_W (.E_in(ACC_e), .D_x(_5bitpc2_1_pc_out), .E_out(1'b1), .Q_x({Acc_W_q_x_2, Acc_W_q_x}));
  LED led_3 (.in(ALU_RSLTe));
  sapRegX Reg_B (.E_in(ALU_RSLTe), .D_x(_5bitpc2_1_pc_out), .E_out(1'b1), .Q_x(Reg_B_q_x));
  sapRegX Reg_I_2 (.E_in(ADDRRam_e), .D_x(_5bitpc2_1_pc_out), .E_out(1'b1), .Q_x(Reg_I_2_q_x));
  Seven_Seg_Hex seven_seg_hex_8 (.d(Acc_W_q_x), .dp(1'b0));
  Seven_Seg_Hex seven_seg_hex_9 (.d(Reg_I_2_q_x[7:4]), .dp(1'b0));
  sapALU_1 sapalu_1_1 (
    .nINV(ALU_INV), .CY(ALU_CYin), .A({Acc_W_q_x_2, Acc_W_q_x}), .B(Reg_B_q_x), .SUB(ALU_SUB), .Flg_Z(FLG_z),
    .Flg_Neg(FLG_neg), .O(ALU_dsp));  // open: C_out
  Seven_Seg_Hex seven_seg_hex_10 (.d(Reg_I_2_q_x[3:0]), .dp(1'b0));
  Seven_Seg_Hex seven_seg_hex_11 (.d(ALU_dsp[7:4]), .dp(1'b0));
  LED led_4 (.in(ALU_OUTe));
  Seven_Seg_Hex seven_seg_hex_12 (.d(ALU_dsp[3:0]), .dp(1'b0));
  assign _5bitpc2_1_pc_out = ALU_OUTe ? ALU_dsp : 8'bz;  // Driver driver_2
  RAMDualPort #(.AddrBits(8), .Bits(8)) ramdualport_1 (
    .A(Reg_I_2_q_x), .Din(_5bitpc2_1_pc_out), .str(RAM_e), .C(Base_Clk), .ld(RAMRD_e), .D(_5bitpc2_1_pc_out));
  PullUp #(.Bits(8)) pullup_1 (.out(_5bitpc2_1_pc_out));

  // Other names for the same wires on the sheet: Clk = Base_Clk

  // Notes on the sheet:
  //   Formato da instrução
  //   OOOOAAAAAAAA
  //   OOOO -> Codigo de instrucao
  //   AAAAAAAA -->> Endereco do operando / valor
  //   Codigo
  //   da Instrucao
  //   contents of PGM_mem (hex, n*v repeats v):
  //   223,331,112,131,272,335,247,135,257,f
  //   contents of MicroCodigo (hex, n*v repeats v):
  //   2014,2002,2008,5*0,2014,2060,2,2008,4*0,2014,a420,2002,2008,4*0
  //   ,2014,20a0,2002,2008,4*0,2014,2060,2480,2,2008,0,0,0,2014,2060
  //   ,2500,2,2008,0,0,0,2014,2060,3500,2,2008,0,0,0,2014,2060,a600
  //   ,2002,2008,0,0,0,2014,21,2008,5*0,2014,2,12020,2008,4*0,2014,2
  //   ,22020,2008,4*0,2014,2002,2008,5*0,2014,2002,2008,5*0,2014,2002
  //   ,2008,5*0,2014,2002,2008,5*0,2014,2008
  //   @Instrucao
  //   T(x)
  //   da microinstrucao
  //   Barramento
  //   Acumulador
  //   @Memoria RAM
endmodule
