// Digital circuit sap1pc.dig as structural Verilog
module sap1pc (
  input  CLR,
  input  Cp,
  input  nClk,
  input  Ep,
  input  clk,
  output AI0,
  output AI1,
  output AI2,
  output AI3
);

  wire and_1_out, and_2_out, and_3_out;
  wire [3:0] jk_ff_as_1_q;

  JK_FF_AS jk_ff_as_1 (.Set(1'b0), .J(Cp), .C(clk), .K(Cp), .Clr(CLR), .Q(jk_ff_as_1_q[0]));  // open: nQ
  and and_1 (and_1_out, Cp, jk_ff_as_1_q[0]);
  assign AI0 = Ep ? jk_ff_as_1_q[0] : 1'bz;  // Driver driver_1
  JK_FF_AS jk_ff_as_2 (.Set(1'b0), .J(and_1_out), .C(clk), .K(and_1_out), .Clr(CLR), .Q(jk_ff_as_1_q[1]));  // open: nQ
  and and_2 (and_2_out, Cp, and_1_out, jk_ff_as_1_q[1]);
  assign AI1 = Ep ? jk_ff_as_1_q[1] : 1'bz;  // Driver driver_2
  JK_FF_AS jk_ff_as_3 (.Set(1'b0), .J(and_2_out), .C(clk), .K(and_2_out), .Clr(CLR), .Q(jk_ff_as_1_q[2]));  // open: nQ
  and and_3 (and_3_out, Cp, and_2_out, jk_ff_as_1_q[2]);
  assign AI2 = Ep ? jk_ff_as_1_q[2] : 1'bz;  // Driver driver_3
  JK_FF_AS jk_ff_as_4 (.Set(1'b0), .J(and_3_out), .C(clk), .K(and_3_out), .Clr(CLR), .Q(jk_ff_as_1_q[3]));  // open: nQ
  assign AI3 = Ep ? jk_ff_as_1_q[3] : 1'bz;  // Driver driver_4
  Seven_Seg_Hex seven_seg_hex_1 (.d(jk_ff_as_1_q), .dp(clk));
endmodule
