// Digital circuit sapALU0.dig as structural Verilog
module sapALU0 (
  input  CY_in,
  input  A,
  input  B,
  input  INV,
  output S,
  output CY_ou
);

  wire and_1_out, and_2_out, xor_1_out, xor_2_out;

  xor xor_1 (xor_1_out, B, INV);
  xor xor_2 (xor_2_out, A, xor_1_out);
  and and_1 (and_1_out, A, xor_1_out);
  xor xor_3 (S, CY_in, xor_2_out);
  and and_2 (and_2_out, CY_in, xor_2_out);
  or or_1 (CY_ou, and_2_out, and_1_out);
endmodule
