// Digital circuit sapALU_1.dig as structural Verilog
module sapALU_1 (
  input  nINV,
  input  CY,
  input  [7:0] A,
  input  [7:0] B,
  input  SUB,
  output C_out,
  output Flg_Z,
  output Flg_Neg,
  output [7:0] O
);

  wire or_1_out, sapalu0_1_cy_ou, sapalu0_2_cy_ou, sapalu0_3_cy_ou, sapalu0_4_cy_ou, sapalu0_5_cy_ou,
       sapalu0_6_cy_ou, sapalu0_7_cy_ou, xor_1_out;

  or or_1 (or_1_out, CY, SUB);
  sapALU0 sapalu0_1 (.CY_in(or_1_out), .A(A[0]), .B(B[0]), .SUB(SUB), .nINV(nINV), .S(O[0]), .CY_ou(sapalu0_1_cy_ou));
  sapALU0 sapalu0_2 (
    .CY_in(sapalu0_1_cy_ou), .A(A[1]), .B(B[1]), .SUB(SUB), .nINV(nINV), .S(O[1]), .CY_ou(sapalu0_2_cy_ou));
  sapALU0 sapalu0_3 (
    .CY_in(sapalu0_2_cy_ou), .A(A[2]), .B(B[2]), .SUB(SUB), .nINV(nINV), .S(O[2]), .CY_ou(sapalu0_3_cy_ou));
  sapALU0 sapalu0_4 (
    .CY_in(sapalu0_3_cy_ou), .A(A[3]), .B(B[3]), .SUB(SUB), .nINV(nINV), .S(O[3]), .CY_ou(sapalu0_4_cy_ou));
  sapALU0 sapalu0_5 (
    .CY_in(sapalu0_4_cy_ou), .A(A[4]), .B(B[4]), .SUB(SUB), .nINV(nINV), .S(O[4]), .CY_ou(sapalu0_5_cy_ou));
  sapALU0 sapalu0_6 (
    .CY_in(sapalu0_5_cy_ou), .A(A[5]), .B(B[5]), .SUB(SUB), .nINV(nINV), .S(O[5]), .CY_ou(sapalu0_6_cy_ou));
  sapALU0 sapalu0_7 (
    .CY_in(sapalu0_6_cy_ou), .A(A[6]), .B(B[6]), .SUB(SUB), .nINV(nINV), .S(O[6]), .CY_ou(sapalu0_7_cy_ou));
  sapALU0 sapalu0_8 (.CY_in(sapalu0_7_cy_ou), .A(A[7]), .B(B[7]), .SUB(SUB), .nINV(nINV), .S(O[7]), .CY_ou(C_out));
  xor xor_1 (xor_1_out, SUB, C_out);
  Seven_Seg_Hex seven_seg_hex_1 (.d(A[3:0]), .dp(1'b0));
  Seven_Seg_Hex seven_seg_hex_2 (.d(A[7:4]), .dp(1'b0));
  Seven_Seg_Hex seven_seg_hex_3 (.d(O[3:0]), .dp(1'b0));
  Seven_Seg_Hex seven_seg_hex_4 (.d(O[7:4]), .dp(1'b0));
  nor nor_1 (Flg_Z, O[0], O[1], O[2], O[3], O[4], O[5], O[6], O[7]);
  and and_1 (Flg_Neg, SUB, xor_1_out);
  Seven_Seg_Hex seven_seg_hex_5 (.d(B[3:0]), .dp(1'b0));
  Seven_Seg_Hex seven_seg_hex_6 (.d(B[7:4]), .dp(1'b0));

  // Other names for the same wires on the sheet: RA[7:0] = A; RB[7:0] = B

  // Notes on the sheet:
  //   nINV: default 1
endmodule
